# Fritzing sketch ClientSketch (saved by Fritzing 0.8.7b)
breadboards: 1

parts:
  Parte1 = Arduino Uno (Rev3)
  Mod1 = Dragino LoRa Shield V1.4
  ANT1 = Antenna  # not connected
  R2 = Photocell (LDR) [package=THT]
  R3 = Resistor [package="0402 [SMD]"]
  S1 = Pushbutton [package="[THT]"]
  LED1 = smd LED [color="Red (633nm)" package="0603 [SMD]"]
  R4 = Resistor [package="0402 [SMD]"]

nets:
  N1: Parte1.A0, Mod1.A0, R2.pin_1, R3.Pin_0
  N2: Parte1.A1, Mod1.A1
  N3: Parte1.A2, Mod1.A2
  N4: Parte1.A3, Mod1.A3
  N5: Parte1.A4/SDA, Mod1.A4, Mod1.SDA
  N6: Parte1.A5/SCL, Mod1.A5, Mod1.SCL
  N7: Parte1.D8, Mod1.8
  N8: Parte1.D9_PWM, Mod1.9
  N9: Parte1.D10_PWM/SS, Mod1.10
  N10: Parte1.D11_PWM/MOSI, Mod1.D11, Mod1.11
  N11: Parte1.D12/MISO, Mod1.12
  N12: Parte1.D13/SCK, Mod1.D13, Mod1.13
  GND: Parte1.GND, Mod1.GND, Mod1.ICSP1_GND, R3.Pin_1, S1.Pin_1, S1.Pin_2, LED1.anode
  N13: Parte1.AREF, Mod1.AREF
  N14: Parte1.D0/RX, Mod1.0
  N15: Parte1.D1/TX, Mod1.1
  N16: Parte1.D2, Mod1.DIO0, Mod1.2
  N17: Parte1.D3_PWM, Mod1.3
  N18: Parte1.D4, Mod1.4, S1.Pin_3, S1.Pin_4
  N19: Parte1.D5_PWM, Mod1.5, R4.Pin_1
  N20: Parte1.D6_PWM, Mod1.6
  N21: Parte1.D7, Mod1.7
  N22: Parte1.ioref, Mod1.IOREF
  N23: Parte1.RESET, Mod1.RST
  3V3: Parte1.3V3, Mod1.3V3
  5V: Parte1.5V, Mod1.5V, R2.pin_0
  VIN: Parte1.VIN, Mod1.VIN
  N24: Parte1.N/C, Mod1.NC
  N25: LED1.cathode, R4.Pin_0
